# Fritzing sketch intimatron (saved by Fritzing 0.8.7b)
circuit board: 5.31421cm x 13.2727cm
circuit board: 5.5cm x 6.5cm

parts:
  Componente1 = Arduino Mega 2560 (Rev3)
  T1-RJ9 = RJ9 [package=rj9]
  T1-LCD-LED = molex pin header, 2 pins [form=molex]
  T1-R1 = TRIMPOT [package=3362u-2]
  T2-KEY = shrouded pin header, 26 pins [form="♂ (shrouded male)"]
  T1-KEY = shrouded pin header, 26 pins [form="♂ (shrouded male)"]
  T2-RJ9 = RJ9 [package=rj9]
  T1-HOOK = molex pin header, 5 pins [form=molex]
  T1-PHONE = male pin header, 2 pins [form="♂ (male)"]
  T1-J2_1 = shrouded pin header, 14 pins [form="♂ (shrouded male)"]
  T1-J2_2 = shrouded pin header, 14 pins [form="♂ (shrouded male)"]
  Q1 = PNP-Transistor [package="TO92 [THT]"]
  J1 = female pin header, 2 pins [form="♀ (female)"]
  R1 = Resistor [tolerance=±5% resistance=100 package=THT]
  R2 = Resistor [tolerance=±5% resistance=1k package=THT]
  R3 = Resistor [tolerance=±5% resistance=50 package=THT]
  Q2 = PNP-Transistor [package="TO92 [THT]"]
  J2 = female pin header, 2 pins [form="♀ (female)"]
  R4 = Resistor [tolerance=±5% resistance=50 package=THT]
  R5 = Resistor [tolerance=±5% resistance=100 package=THT]
  R6 = Resistor [tolerance=±5% resistance=1k package=THT]
  T2-LCD-LED = molex pin header, 2 pins [form=molex]
  T1-R2 = TRIMPOT [package=3362u-2]
  T2-HOOK = molex pin header, 5 pins [form=molex]
  T2-J2_2 = shrouded pin header, 14 pins [form="♂ (shrouded male)"]
  T2-PHONE = male pin header, 2 pins [form="♂ (male)"]
  T2-J2_1 = shrouded pin header, 14 pins [form="♂ (shrouded male)"]
  T3-PHONE = male pin header, 2 pins [form="♂ (male)"]
  Q3 = PNP-Transistor [package="TO92 [THT]"]
  J3 = female pin header, 2 pins [form="♀ (female)"]
  R7 = Resistor [tolerance=±5% resistance=50 package=THT]
  R8 = Resistor [tolerance=±5% resistance=100 package=THT]
  R9 = Resistor [tolerance=±5% resistance=1k package=THT]
  T3-KEY = shrouded pin header, 26 pins [form="♂ (shrouded male)"]
  T3-LCD-LED = molex pin header, 2 pins [form=molex]
  T3-HOOK = molex pin header, 5 pins [form=molex]
  T3-RJ9 = RJ9 [package=rj9]  # not connected
  T3-J2_1 = shrouded pin header, 14 pins [form="♂ (shrouded male)"]
  T3-J2_2 = shrouded pin header, 14 pins [form="♂ (shrouded male)"]
  T1-R3 = TRIMPOT [package=3362u-2]
  T4-PHONE = male pin header, 2 pins [form="♂ (male)"]
  Q4 = PNP-Transistor [package="TO92 [THT]"]
  J4 = female pin header, 2 pins [form="♀ (female)"]
  R10 = Resistor [tolerance=±5% resistance=50 package=THT]
  R11 = Resistor [tolerance=±5% resistance=100 package=THT]
  R12 = Resistor [tolerance=±5% resistance=1k package=THT]
  T4-KEY = shrouded pin header, 26 pins [form="♂ (shrouded male)"]
  T4-LCD-LED = molex pin header, 2 pins [form=molex]
  T4-HOOK = molex pin header, 5 pins [form=molex]
  T4-RJ9 = RJ9 [package=rj9]
  T4-J2_1 = shrouded pin header, 14 pins [form="♂ (shrouded male)"]
  T4-J2_2 = shrouded pin header, 14 pins [form="♂ (shrouded male)"]
  T1-R4 = TRIMPOT [package=3362u-2]
  T5-PHONE = male pin header, 2 pins [form="♂ (male)"]
  Q5 = PNP-Transistor [package="TO92 [THT]"]
  J5 = female pin header, 2 pins [form="♀ (female)"]
  R13 = Resistor [tolerance=±5% resistance=50 package=THT]
  R14 = Resistor [tolerance=±5% resistance=100 package=THT]
  R15 = Resistor [tolerance=±5% resistance=1k package=THT]
  T5-KEY = shrouded pin header, 26 pins [form="♂ (shrouded male)"]
  T5-LCD-LED = molex pin header, 2 pins [form=molex]
  T5-HOOK = molex pin header, 5 pins [form=molex]
  T5-RJ9 = RJ9 [package=rj9]
  T5-J2_1 = shrouded pin header, 14 pins [form="♂ (shrouded male)"]
  T5-J2_2 = shrouded pin header, 14 pins [form="♂ (shrouded male)"]
  T1-R5 = TRIMPOT [package=3362u-2]
  R16 = Resistor [tolerance=±5% resistance=1k package=THT]
  R17 = Resistor [tolerance=±5% resistance=1k package=THT]
  Reset_-_S1 = Pushbutton [package="[THT]"]
  R18 = Resistor [tolerance=±5% resistance=100 package=THT]
  LED1 = LED - 5mm [color="Red (633nm)" package="5 mm [THT]"]
  R19 = Resistor [tolerance=±5% resistance=100 package=THT]
  LED2 = LED - 5mm [color="Red (633nm)" package="5 mm [THT]"]
  R20 = Resistor [tolerance=±5% resistance=100 package=THT]
  LED3 = LED - 5mm [color="Red (633nm)" package="5 mm [THT]"]
  R21 = Resistor [tolerance=±5% resistance=100 package=THT]
  LED4 = LED - 5mm [color="Red (633nm)" package="5 mm [THT]"]
  R22 = Resistor [tolerance=±5% resistance=150 package=THT]
  LED5 = LED - 5mm [color="Red (633nm)" package="5 mm [THT]"]

nets:
  T3-KC1: Componente1.A8, T3-KEY.pin12, T3-J2_1.pin4, T3-J2_2.pin4
  T3-KC2: Componente1.A9, T3-KEY.pin11, T3-J2_1.pin5, T3-J2_2.pin5
  T3-KC3: Componente1.A10, T3-KEY.pin10, T3-J2_1.pin6, T3-J2_2.pin6
  T3-KC4: Componente1.A11, T3-KEY.pin9, T3-J2_1.pin7, T3-J2_2.pin7
  T2-KL1: Componente1.A12, T2-KEY.pin18, T2-J2_2.pin8, T2-J2_1.pin8
  T2-KL2: Componente1.A13, T2-KEY.pin17, T2-J2_2.pin9, T2-J2_1.pin9
  T2-KL4: Componente1.A14, T2-KEY.pin15, T2-J2_2.pin11, T2-J2_1.pin11
  T2-KL3: Componente1.A15, T2-KEY.pin16, T2-J2_2.pin10, T2-J2_1.pin10
  T3-DISP-A: Componente1.A6, R7.Pin_0, T3-J2_1.pin2, T3-J2_2.pin2
  T3-HOOK: Componente1.A7, T3-HOOK.pin1, T3-J2_1.pin3, T3-J2_2.pin3
  T5-KC1: Componente1.D21/SCL, Componente1.SCL, T5-KEY.pin12, T5-J2_1.pin4, T5-J2_2.pin4
  T5-KC2: Componente1.D20/SDA, Componente1.SDA, T5-KEY.pin11, T5-J2_1.pin5, T5-J2_2.pin5
  T5-KC3: Componente1.D19/RX1, T5-KEY.pin10, T5-J2_1.pin6, T5-J2_2.pin6
  T5-KC4: Componente1.D18/TX1, T5-KEY.pin9, T5-J2_1.pin7, T5-J2_2.pin7
  T5-KL1: Componente1.D17_PWM/RX2, T5-KEY.pin18, T5-J2_1.pin8, T5-J2_2.pin8
  T5-KL2: Componente1.D16_PWM/TX2, T5-KEY.pin17, T5-J2_1.pin9, T5-J2_2.pin9
  T5-KL3: Componente1.D15/RX3, T5-KEY.pin16, T5-J2_1.pin10, T5-J2_2.pin10
  T5-KL4: Componente1.D14/TX3, T5-KEY.pin15, T5-J2_1.pin11, T5-J2_2.pin11
  GND/T1-DISP-K/T2-DISP-K/T3-DISP-K/T4-DISP-K/T5-DISP-K: Componente1.GND, T1-R1.WIPER, T1-R1.CW, T1-HOOK.pin2, T1-J2_1.pin14, T1-J2_2.pin14, T1-R2.WIPER, T1-R2.CW, T2-HOOK.pin2, T2-J2_2.pin14, T2-J2_1.pin14, T3-HOOK.pin2, T3-J2_1.pin14, T3-J2_2.pin14, T1-R3.WIPER, T1-R3.CW, T4-HOOK.pin2, T4-J2_1.pin14, T4-J2_2.pin14, T1-R4.WIPER, T1-R4.CW, T5-HOOK.pin2, T5-J2_1.pin14, T5-J2_2.pin14, T1-R5.WIPER, T1-R5.CW, Reset_-_S1.Pin_3, Reset_-_S1.Pin_4, LED1.cathode, LED2.cathode, LED3.cathode, LED4.cathode, LED5.cathode
  N1: Componente1.D12_PWM, R18.Pin_0
  N2: Componente1.D11_PWM, R19.Pin_0
  N3: Componente1.D10_PWM, R20.Pin_0
  N4: Componente1.D9_PWM, R21.Pin_0
  N5: Componente1.D8_PWM, R22.Pin_0
  N6: Componente1.RESET, Reset_-_S1.Pin_1, Reset_-_S1.Pin_2
  5V: Componente1.5V, T1-J2_1.pin1, T1-J2_2.pin1, R1.Pin_1, R5.Pin_1, T2-J2_2.pin1, T2-J2_1.pin1, R8.Pin_1, T3-J2_1.pin1, T3-J2_2.pin1, R11.Pin_1, T4-J2_1.pin1, T4-J2_2.pin1, R14.Pin_1, T5-J2_1.pin1, T5-J2_2.pin1, R16.Pin_0, R17.Pin_0
  T5-HOOK: Componente1.D22, T5-HOOK.pin1, T5-J2_1.pin3, T5-J2_2.pin3
  T1-DISP-A: Componente1.D23, T1-J2_1.pin2, T1-J2_2.pin2, R2.Pin_0, R3.Pin_0
  T5-DISP-A: Componente1.D24, R13.Pin_0, R15.Pin_0, T5-J2_1.pin2, T5-J2_2.pin2
  T1-HOOK: Componente1.D25, T1-HOOK.pin1, T1-J2_1.pin3, T1-J2_2.pin3, R17.Pin_1
  T4-KL4: Componente1.D26, T4-KEY.pin15, T4-J2_1.pin11, T4-J2_2.pin11
  T1-KC1: Componente1.D27, T1-KEY.pin12, T1-J2_1.pin4, T1-J2_2.pin4
  T4-KL3: Componente1.D28, T4-KEY.pin16, T4-J2_1.pin10, T4-J2_2.pin10
  T1-KC2: Componente1.D29, T1-J2_1.pin5
  T4-KL2: Componente1.D30, T4-KEY.pin17, T4-J2_1.pin9, T4-J2_2.pin9
  T1-KC3: Componente1.D31, T1-KEY.pin10, T1-J2_1.pin6, T1-J2_2.pin6
  T4-KL1: Componente1.D32, T4-KEY.pin18, T4-J2_1.pin8, T4-J2_2.pin8
  T1-KC4: Componente1.D33, T1-KEY.pin9, T1-J2_1.pin7, T1-J2_2.pin7
  T4-KC4: Componente1.D34, T4-KEY.pin9, T4-J2_1.pin7, T4-J2_2.pin7
  T1-KL1: Componente1.D35, T1-KEY.pin18, T1-J2_1.pin8, T1-J2_2.pin8
  T4-KC3: Componente1.D36, T4-KEY.pin10, T4-J2_1.pin6, T4-J2_2.pin6
  T1-KL2: Componente1.D37, T1-KEY.pin17, T1-J2_1.pin9, T1-J2_2.pin9
  T4-KC2: Componente1.D38, T4-KEY.pin11, T4-J2_1.pin5, T4-J2_2.pin5
  T1-KL3: Componente1.D39, T1-KEY.pin16, T1-J2_1.pin10, T1-J2_2.pin10
  T4-KC1: Componente1.D40, T4-KEY.pin12, T4-J2_1.pin4, T4-J2_2.pin4
  T1-KL4: Componente1.D41, T1-KEY.pin15, T1-J2_1.pin11, T1-J2_2.pin11
  T4-HOOK: Componente1.D42, T4-HOOK.pin1, T4-J2_1.pin3, T4-J2_2.pin3
  T2-DISP-A: Componente1.D43, R4.Pin_0, R6.Pin_0, T2-J2_2.pin2, T2-J2_1.pin2
  T4-DISP-A: Componente1.D44, R10.Pin_0, R12.Pin_0, T4-J2_1.pin2, T4-J2_2.pin2
  T2-HOOK: Componente1.D45, T2-HOOK.pin1, T2-J2_2.pin3, T2-J2_1.pin3, R16.Pin_1
  T3-KL4: Componente1.D46, T3-KEY.pin15, T3-J2_1.pin11, T3-J2_2.pin11
  T2-KC1: Componente1.D47, T2-KEY.pin12, T2-J2_2.pin4, T2-J2_1.pin4
  T3-KL3: Componente1.D48, T3-KEY.pin16, T3-J2_1.pin10, T3-J2_2.pin10
  T2-KC2: Componente1.D49, T2-KEY.pin11, T2-J2_2.pin5, T2-J2_1.pin5
  T3-KL2: Componente1.D50, T3-KEY.pin17, T3-J2_1.pin9, T3-J2_2.pin9
  T2-KC3: Componente1.D51, T2-KEY.pin10, T2-J2_2.pin6, T2-J2_1.pin6
  T3-KL1: Componente1.D52, T3-KEY.pin18, T3-J2_1.pin8, T3-J2_2.pin8
  T2-KC4: Componente1.D53, T2-KEY.pin9, T2-J2_2.pin7, T2-J2_1.pin7
  T1-PHONE-GND: T1-RJ9.3, T1-PHONE.pin1, T1-J2_1.pin13, T1-J2_2.pin13
  T1-PHONE: T1-RJ9.4, T1-PHONE.pin2, T1-J2_1.pin12, T1-J2_2.pin12
  N7: T1-LCD-LED.pin1, T1-R1.CCW
  N8: T1-LCD-LED.pin2, Q1.C, J1.pin2
  N9: T1-KEY.pin11, T1-J2_2.pin5
  T2-PHONE-GND: T2-RJ9.3, T2-J2_2.pin13, T2-PHONE.pin1, T2-J2_1.pin13
  T2-PHONE: T2-RJ9.4, T2-J2_2.pin12, T2-PHONE.pin2, T2-J2_1.pin12
  N10: Q1.E, R1.Pin_0
  N11: Q1.B, R2.Pin_1
  N12: J1.pin1, R3.Pin_1
  N13: Q2.E, R5.Pin_0
  N14: Q2.B, R6.Pin_1
  N15: Q2.C, J2.pin2, T2-LCD-LED.pin2
  N16: J2.pin1, R4.Pin_1
  N17: T2-LCD-LED.pin1, T1-R2.CCW
  T3-PHONE-GND: T3-PHONE.pin1, T3-J2_1.pin13, T3-J2_2.pin13
  T3-PHONE: T3-PHONE.pin2, T3-J2_1.pin12, T3-J2_2.pin12
  N18: Q3.E, R8.Pin_0
  N19: Q3.B, R9.Pin_1
  N20: Q3.C, J3.pin2, T3-LCD-LED.pin2
  N21: J3.pin1, R7.Pin_1
  N22: T3-LCD-LED.pin1, T1-R3.CCW
  T4-PHONE-GND: T4-PHONE.pin1, T4-RJ9.1, T4-J2_1.pin13, T4-J2_2.pin13
  T4-PHONE: T4-PHONE.pin2, T4-RJ9.2, T4-J2_1.pin12, T4-J2_2.pin12
  N23: Q4.E, R11.Pin_0
  N24: Q4.B, R12.Pin_1
  N25: Q4.C, J4.pin2, T4-LCD-LED.pin2
  N26: J4.pin1, R10.Pin_1
  N27: T4-LCD-LED.pin1, T1-R4.CCW
  T5-PHONE-GND: T5-PHONE.pin1, T5-RJ9.1, T5-J2_1.pin13, T5-J2_2.pin13
  T5-PHONE: T5-PHONE.pin2, T5-RJ9.2, T5-J2_1.pin12, T5-J2_2.pin12
  N28: Q5.E, R14.Pin_0
  N29: Q5.B, R15.Pin_1
  N30: Q5.C, J5.pin2, T5-LCD-LED.pin2
  N31: J5.pin1, R13.Pin_1
  N32: T5-LCD-LED.pin1, T1-R5.CCW
  N33: R18.Pin_1, LED1.anode
  N34: R19.Pin_1, LED2.anode
  N35: R20.Pin_1, LED3.anode
  N36: R21.Pin_1, LED4.anode
  N37: R22.Pin_1, LED5.anode

notes:
  Gancho
  LED
  AUDIO - 1
  AUDIO - 2
  AUDIO - 3
  AUDIO - 4
  AUDIO - 5
  Fone
  http://www.carlosdelfino.eti.br
  Intimatron - Phone - V0.2
  Intimatron - Shield - V0.4
  Obs. a sequência A14, A15
  Reset
